// Logisim project FinalCircuit.circ as structural Verilog: 31 circuits, main circuit main
module main (
);

  wire ALU_zero, BranchChecker_branchtaken, button_1_out, clock_1_out, Decoder_immtoalu, Decoder_led,
       Decoder_memread, Decoder_memtoreg, Decoder_memwrite, Decoder_regwrite, Decoder_writeled,
       Decoder_zerostoalu, ex_mem_1_alu0_out, ex_mem_1_led_out, ex_mem_1_memtoreg_out, ex_mem_1_memwrite_out,
       ex_mem_1_writeen_out, ex_mem_1_writeled_out, haltdecoder_yasser_1_halt, id_ex_1_immtoalu_out,
       id_ex_1_led_out, id_ex_1_memread_out, id_ex_1_memtoreg_out, id_ex_1_memwrite_out, id_ex_1_writeen_out,
       id_ex_1_writeled_out, id_ex_1_zerostoalu_out, Instruction_Splitter_subop,
       Instruction_Splitter_unsigned, mem_wb_1_led_out, mem_wb_1_memtoreg_out, mem_wb_1_writeen_out,
       mem_wb_1_writeled_out, not_1_out, register_1_q, ResultToLess_less,
       storeforwardingunit_1_towritedatamux;
  wire [1:0] forwardingunit_main_1_tomuxa, forwardingunit_main_1_tomuxb;
  wire [2:0] ex_mem_1_rs2_out, ex_mem_1_rs_out, id_ex_1_rs2_out, id_ex_1_rs_out,
       Instruction_Splitter_readregister1, Instruction_Splitter_readregister2, mem_wb_1_rs_out;
  wire [3:0] Decoder_aluop, id_ex_1_aluop_out, Instruction_Splitter_opcode;
  wire [7:0] adder_1_out, Instruction_Splitter_immediate, multiplexer_1_out, PC_q, RegistertoAddress_address;
  wire [15:0] ALU_result, ex_mem_1_aluresult_out, ex_mem_1_register1_out, ex_mem_1_register2_out,
       id_ex_1_register1_out, id_ex_1_register2_out, id_ex_1_signextended_out, IF_ID_to_instruction_splitter,
       mem_wb_1_aluresult_out, mem_wb_1_data_out, mem_wb_1_register1_out, multiplexer_2_out,
       multiplexer_3_out, multiplexer_4_out, multiplexer_5_out, multiplexer_6_out, multiplexer_7_out,
       ram_1_data, register_2_q, Registers_readdata1, Registers_readdata2, rom_1_data,
       Sign_Extend_signextendedimm;

  not not_1 (not_1_out, haltdecoder_yasser_1_halt);
  Register PC (.D(multiplexer_1_out), .en(not_1_out), .Q(PC_q), .clk(clock_1_out), .clr(button_1_out));
  Button button_1 (.out(button_1_out));
  Adder adder_1 (.a(PC_q), .b(8'h1), .out(adder_1_out));  // open: cin, cout
  ROM #(.dataWidth(16)) rom_1 (.addr(PC_q), .data(rom_1_data), .sel(1'b1));
  HaltDecoder_Yasser haltdecoder_yasser_1 (.Opcode(rom_1_data), .Halt(haltdecoder_yasser_1_halt));  // open: LED
  IF_ID IF_ID (
    .From_Instruction_Memory(rom_1_data), .Clock(clock_1_out), .Bubble(register_1_q),
    .To_Instruction_Splitter(IF_ID_to_instruction_splitter));
  Register #(.width(1)) register_1 (
    .D(BranchChecker_branchtaken), .Q(register_1_q), .clk(clock_1_out));  // open: en, clr
  BranchCheck BranchChecker (
    .RS(Registers_readdata1), .OPCode(Instruction_Splitter_opcode), .BranchTaken(BranchChecker_branchtaken));
  InstructionSplitter Instruction_Splitter (
    .Instruction(IF_ID_to_instruction_splitter), .Opcode(Instruction_Splitter_opcode),
    .ReadRegister1(Instruction_Splitter_readregister1), .ReadRegister2(Instruction_Splitter_readregister2),
    .SubOp(Instruction_Splitter_subop), .Unsigned(Instruction_Splitter_unsigned),
    .Immediate(Instruction_Splitter_immediate));  // open: WriteRegister, ShiftAmount
  ResultToLess ResultToLess (.Result(ALU_result), .Less(ResultToLess_less));
  Clock clock_1 (.out(clock_1_out));
  SignExtend Sign_Extend (
    .Unsigned(Instruction_Splitter_unsigned), .Immediate(Instruction_Splitter_immediate),
    .SignExtendedImm(Sign_Extend_signextendedimm));
  Decoder Decoder (
    .Opcode(Instruction_Splitter_opcode), .Subop(Instruction_Splitter_subop), .Zero(ALU_zero),
    .Less(ResultToLess_less), .RegWrite(Decoder_regwrite), .ALUOp(Decoder_aluop),
    .IMMtoALU(Decoder_immtoalu), .ZerosToALU(Decoder_zerostoalu), .MemWrite(Decoder_memwrite),
    .MemtoReg(Decoder_memtoreg), .LED(Decoder_led), .WriteLED(Decoder_writeled), .MemRead(Decoder_memread));  // open: ShiftSrc, ShifterToReg, RegtoPC, IMMtoPC, Halt, PCtoReg
  Multiplexer #(.width(8), .disabled(0), .enable("false")) multiplexer_1 (
    .in0(adder_1_out), .in1(Instruction_Splitter_immediate), .out(multiplexer_1_out),
    .sel(BranchChecker_branchtaken));
  RegisterFile Registers (
    .ReadRegister1(Instruction_Splitter_readregister1), .ReadRegister2(Instruction_Splitter_readregister2),
    .WriteRegister(mem_wb_1_rs_out), .WriteData(multiplexer_7_out), .WriteEnable(mem_wb_1_writeen_out),
    .Clock(clock_1_out), .ReadData1(Registers_readdata1), .ReadData2(Registers_readdata2));
  ID_EX id_ex_1 (
    .ShiftSrc_IN(Instruction_Splitter_readregister2), .Register1_IN(Registers_readdata1),
    .Register2_IN(Registers_readdata2), .SignExtended_IN(Sign_Extend_signextendedimm),
    .ALUop_IN(Decoder_aluop), .IMMtoALU_IN(Decoder_immtoalu), .ZerosToALU_IN(Decoder_zerostoalu),
    .MemWrite_IN(Decoder_memwrite), .MemToReg_IN(Decoder_memtoreg), .LED_IN(Decoder_led),
    .WriteLED_IN(Decoder_writeled), .RS_IN(Instruction_Splitter_readregister1), .MemRead_IN(Decoder_memread),
    .WriteEn_IN(Decoder_regwrite), .clk(clock_1_out), .RS2_OUT(id_ex_1_rs2_out),
    .Register1_OUT(id_ex_1_register1_out), .Register2_OUT(id_ex_1_register2_out),
    .SignExtended_OUT(id_ex_1_signextended_out), .ALUop_OUT(id_ex_1_aluop_out),
    .IMMtoALU_OUT(id_ex_1_immtoalu_out), .ZerosToALU_OUT(id_ex_1_zerostoalu_out),
    .MemWrite_OUT(id_ex_1_memwrite_out), .MemToReg_OUT(id_ex_1_memtoreg_out), .LED_OUT(id_ex_1_led_out),
    .WriteLED_OUT(id_ex_1_writeled_out), .RS_OUT(id_ex_1_rs_out), .MemRead_OUT(id_ex_1_memread_out),
    .WriteEn_OUT(id_ex_1_writeen_out));  // open: ShifterToReg_IN, Immediate_IN, RegtoPC_IN, IMMtoPC_IN, PC_1_IN, ShiftAmount_IN, Halt_IN, SubOp_IN, OPCode_IN, PCtoReg_IN, ShifterToReg_OUT, Immediate_OUT, RegtoPC_OUT, IMMtoPC_OUT, PC_1_OUT, ShiftAmount_OUT, Halt_OUT, SubOp_OUT, OPCode_OUT, PCtoReg_OUT
  Multiplexer #(.width(16), .disabled(0), .enable("false")) multiplexer_2 (
    .in0(id_ex_1_register2_out), .in1(id_ex_1_signextended_out), .out(multiplexer_2_out),
    .sel(id_ex_1_immtoalu_out));
  Multiplexer #(.select(2), .width(16), .enable("false")) multiplexer_3 (
    .in0(id_ex_1_register1_out), .in1(multiplexer_7_out), .in2(ex_mem_1_aluresult_out),
    .out(multiplexer_3_out), .sel(forwardingunit_main_1_tomuxa));  // open: in3
  Multiplexer #(.select(2), .width(16), .enable("false")) multiplexer_4 (
    .in0(multiplexer_5_out), .in1(multiplexer_7_out), .in2(ex_mem_1_aluresult_out), .out(multiplexer_4_out),
    .sel(forwardingunit_main_1_tomuxb));  // open: in3
  Multiplexer #(.width(16), .disabled(0), .enable("false")) multiplexer_5 (
    .in0(multiplexer_2_out), .in1({16{1'b0}}), .out(multiplexer_5_out), .sel(id_ex_1_zerostoalu_out));
  ForwardingUnit_Main forwardingunit_main_1 (
    .ID_Ex_rs1(id_ex_1_rs_out), .ID_EX_rs2(id_ex_1_rs2_out), .ex_memRegWrite(ex_mem_1_writeen_out),
    .ex_memWBREG(ex_mem_1_rs_out), .mem_wbRegWrite(mem_wb_1_writeen_out), .mem_wbWBREG(mem_wb_1_rs_out),
    .ToMuxA(forwardingunit_main_1_tomuxa), .ToMuxB(forwardingunit_main_1_tomuxb));
  sixteen_bit_ALU ALU (
    .ALUOperation(id_ex_1_aluop_out), .a(multiplexer_3_out), .b(multiplexer_4_out), .Zero(ALU_zero),
    .Result(ALU_result));  // open: Overflow
  Hex_Digit_Display hex_digit_display_1 (.value(register_2_q[11:8]));  // open: dp
  Hex_Digit_Display hex_digit_display_2 (.value(register_2_q[15:12]));  // open: dp
  Register #(.width(16)) register_2 (
    .D(mem_wb_1_register1_out), .en(mem_wb_1_writeled_out), .Q(register_2_q), .clk(clock_1_out));  // open: clr
  LED Halt (.in(mem_wb_1_led_out));
  EX_MEM ex_mem_1 (
    .Register1_IN(multiplexer_3_out), .RS2_IN(id_ex_1_rs2_out), .ALUResult_IN(ALU_result),
    .Register2_IN(id_ex_1_register2_out), .MemWrite_IN(id_ex_1_memwrite_out),
    .MemToReg_IN(id_ex_1_memtoreg_out), .LED_IN(id_ex_1_led_out), .WriteLED_IN(id_ex_1_writeled_out),
    .ALU0_IN(id_ex_1_memread_out), .RS_IN(id_ex_1_rs_out), .WriteEn_IN(id_ex_1_writeen_out),
    .clk(clock_1_out), .Register1_OUT(ex_mem_1_register1_out), .RS2_OUT(ex_mem_1_rs2_out),
    .ALUResult_OUT(ex_mem_1_aluresult_out), .Register2_OUT(ex_mem_1_register2_out),
    .MemWrite_OUT(ex_mem_1_memwrite_out), .MemToReg_OUT(ex_mem_1_memtoreg_out), .LED_OUT(ex_mem_1_led_out),
    .WriteLED_OUT(ex_mem_1_writeled_out), .ALU0_OUT(ex_mem_1_alu0_out), .RS_OUT(ex_mem_1_rs_out),
    .WriteEn_OUT(ex_mem_1_writeen_out));  // open: ShifterToReg_IN, PCD_IN, ShiftAmount_IN, SubOp_IN, MemRead_IN, PC_1_IN, PCtoReg_IN, ShifterToReg_OUT, PCD_OUT, ShiftAmount_OUT, SubOp_OUT, MemRead_OUT, PC_1_OUT, PCtoReg_OUT
  Hex_Digit_Display hex_digit_display_3 (.value(register_2_q[7:4]));  // open: dp
  Hex_Digit_Display hex_digit_display_4 (.value(register_2_q[3:0]));  // open: dp
  Multiplexer #(.width(16), .enable("false")) multiplexer_6 (
    .in0(mem_wb_1_data_out), .in1(ex_mem_1_register1_out), .out(multiplexer_6_out),
    .sel(storeforwardingunit_1_towritedatamux));
  ALUtoPC RegistertoAddress (.ALUOut(ex_mem_1_register2_out), .Address(RegistertoAddress_address));
  RAM #(.dataWidth(16), .bus("separate")) ram_1 (
    .addr(RegistertoAddress_address), .din(multiplexer_6_out), .data(ram_1_data),
    .str(ex_mem_1_memwrite_out), .sel(1'b1), .clk(clock_1_out), .ld(ex_mem_1_alu0_out));  // open: clr
  MEM_WB mem_wb_1 (
    .Data_IN(ram_1_data), .ALUResult_IN(ex_mem_1_aluresult_out), .LED_IN(ex_mem_1_led_out),
    .MemToReg_IN(ex_mem_1_memtoreg_out), .Register1_IN(ex_mem_1_register1_out),
    .WriteLED_IN(ex_mem_1_writeled_out), .RS_IN(ex_mem_1_rs_out), .WriteEn_IN(ex_mem_1_writeen_out),
    .clk(clock_1_out), .Data_OUT(mem_wb_1_data_out), .ALUResult_OUT(mem_wb_1_aluresult_out),
    .LED_OUT(mem_wb_1_led_out), .MemToReg_OUT(mem_wb_1_memtoreg_out), .Register1_OUT(mem_wb_1_register1_out),
    .WriteLED_OUT(mem_wb_1_writeled_out), .RS_OUT(mem_wb_1_rs_out), .WriteEn_OUT(mem_wb_1_writeen_out));  // open: ShifterToReg_IN, Shifter_IN, PCD_IN, Extender_IN, MemRead_IN, ShifterToReg_OUT, Shifter_OUT, PCD_OUT, Extender_OUT, MemRead_OUT
  Multiplexer #(.width(16), .disabled(0), .enable("false")) multiplexer_7 (
    .in0(mem_wb_1_aluresult_out), .in1(mem_wb_1_data_out), .out(multiplexer_7_out),
    .sel(mem_wb_1_memtoreg_out));
  StoreForwardingUnit storeforwardingunit_1 (
    .mem_wb_memtoreg(mem_wb_1_memtoreg_out), .mem_wb_WBREG(mem_wb_1_rs_out), .ex_mem_rs2(ex_mem_1_rs2_out),
    .Ex_Mem_memwrite(mem_wb_1_writeen_out), .ToWriteDataMux(storeforwardingunit_1_towritedatamux));

  // Notes on the sheet:
  //   contents of rom_1 (hex, n*v repeats v):
  //   280 640 880 2b00 1404 1204 f600 fa00 7000 97*0 7000
endmodule

module InstructionSplitter (
  input  [15:0] Instruction,
  output [3:0] Opcode,
  output [2:0] ReadRegister1,
  output [2:0] ReadRegister2,
  output [2:0] WriteRegister,
  output [3:0] ShiftAmount,
  output SubOp,
  output Unsigned,
  output [7:0] Immediate
);


  assign Immediate = Instruction[7:0];
  assign Opcode = Instruction[15:12];
  assign ReadRegister1 = Instruction[11:9];
  assign ReadRegister2 = Instruction[8:6];
  assign ShiftAmount = Instruction[4:1];
  assign SubOp = Instruction[0];
  assign Unsigned = Instruction[8];
  assign WriteRegister = Instruction[11:9];
endmodule

module SignExtend (
  input  Unsigned,
  input  [7:0] Immediate,
  output [15:0] SignExtendedImm
);

  wire [15:0] bit_extender_1_out, bit_extender_2_out;

  assign bit_extender_1_out = {{8{Immediate[7]}}, Immediate};  // Bit_Extender bit_extender_1
  assign bit_extender_2_out = {{8{1'b0}}, Immediate};  // Bit_Extender bit_extender_2
  Multiplexer #(.width(16), .disabled(0), .enable("false")) multiplexer_1 (
    .in0(bit_extender_1_out), .in1(bit_extender_2_out), .out(SignExtendedImm), .sel(Unsigned));
endmodule

module ALUtoPC (
  input  [15:0] ALUOut,
  output [7:0] Address
);


  assign Address = ALUOut[7:0];
endmodule

module Shifter (
  input  Subop,
  input  [15:0] Data,
  input  [15:0] ShamtReg,
  input  ShiftSrc,
  input  [3:0] Shamt,
  output [15:0] ShiftOut
);

  wire [3:0] multiplexer_1_out;
  wire [15:0] shifter_1_out, shifter_2_out;

  Multiplexer #(.width(4), .disabled(0), .enable("false")) multiplexer_1 (
    .in0(ShamtReg[3:0]), .in1(Shamt), .out(multiplexer_1_out), .sel(ShiftSrc));
  Shifter_part #(.width(16)) shifter_1 (.in(Data), .\dist (multiplexer_1_out), .out(shifter_1_out));
  Shifter_part #(.width(16), .shift("lr")) shifter_2 (.in(Data), .\dist (multiplexer_1_out), .out(shifter_2_out));
  Multiplexer #(.width(16), .disabled(0), .enable("false")) multiplexer_2 (
    .in0(shifter_1_out), .in1(shifter_2_out), .out(ShiftOut), .sel(Subop));
endmodule

module RegisterFile (
  input  [2:0] ReadRegister1,
  input  [2:0] ReadRegister2,
  input  [2:0] WriteRegister,
  input  [15:0] WriteData,
  input  WriteEnable,
  input  Clock,
  output [15:0] ReadData1,
  output [15:0] ReadData2
);

  wire decoder_1_out0, decoder_1_out1, decoder_1_out2, decoder_1_out3, decoder_1_out4, decoder_1_out5,
       decoder_1_out6, decoder_1_out7;
  wire [15:0] register_1_q, register_2_q, register_3_q, register_4_q, register_5_q, register_6_q,
       register_7_q, register_8_q;

  Decoder_part #(.select(3), .disabled(0)) decoder_1 (
    .out0(decoder_1_out0), .out1(decoder_1_out1), .out2(decoder_1_out2), .out3(decoder_1_out3),
    .out4(decoder_1_out4), .out5(decoder_1_out5), .out6(decoder_1_out6), .out7(decoder_1_out7),
    .sel(WriteRegister), .en(WriteEnable));
  Register #(.width(16)) register_1 (.D(WriteData), .en(decoder_1_out0), .Q(register_1_q), .clk(Clock));  // open: clr
  Register #(.width(16)) register_2 (.D(WriteData), .en(decoder_1_out1), .Q(register_2_q), .clk(Clock));  // open: clr
  Register #(.width(16)) register_3 (.D(WriteData), .en(decoder_1_out2), .Q(register_3_q), .clk(Clock));  // open: clr
  Register #(.width(16)) register_4 (.D(WriteData), .en(decoder_1_out3), .Q(register_4_q), .clk(Clock));  // open: clr
  Register #(.width(16)) register_5 (.D(WriteData), .en(decoder_1_out4), .Q(register_5_q), .clk(Clock));  // open: clr
  Register #(.width(16)) register_6 (.D(WriteData), .en(decoder_1_out5), .Q(register_6_q), .clk(Clock));  // open: clr
  Register #(.width(16)) register_7 (.D(WriteData), .en(decoder_1_out6), .Q(register_7_q), .clk(Clock));  // open: clr
  Register #(.width(16)) register_8 (.D(WriteData), .en(decoder_1_out7), .Q(register_8_q), .clk(Clock));  // open: clr
  Multiplexer #(.select(3), .width(16), .enable("false")) multiplexer_1 (
    .in0(register_1_q), .in1(register_2_q), .in2(register_3_q), .in3(register_4_q), .in4(register_5_q),
    .in5(register_6_q), .in6(register_7_q), .in7(register_8_q), .out(ReadData1), .sel(ReadRegister1));
  Multiplexer #(.select(3), .width(16), .enable("false")) multiplexer_2 (
    .in0(register_1_q), .in1(register_2_q), .in2(register_3_q), .in3(register_4_q), .in4(register_5_q),
    .in5(register_6_q), .in6(register_7_q), .in7(register_8_q), .out(ReadData2), .sel(ReadRegister2));
endmodule

module ShifterDecoder (
  input  [3:0] Opcode,
  output ShiftSrc,
  output ShiftertoReg,
  output RegWrite
);

  and and_1 (RegWrite, ~Opcode[3], Opcode[2], ~Opcode[1]);  // AND_Gate

  assign ShiftertoReg = RegWrite;
  assign ShiftSrc = Opcode[0];
endmodule

module Arith_Log_Decoder (
  input  [3:0] Opcode,
  input  Subop,
  output [3:0] ALUOperation,
  output RegWrite,
  output ALUSrc
);

  wire and_2_out, and_3_out, and_5_out, and_6_out, multiplexer_1_out, not_1_out, not_2_out, not_3_out,
       not_4_out, not_5_out, not_6_out, not_7_out, not_8_out, not_9_out, not_10_out, not_11_out, not_12_out,
       not_13_out, not_14_out, not_15_out, not_16_out, not_17_out, not_18_out, not_19_out, not_20_out,
       not_21_out;

  not not_1 (not_1_out, Opcode[1]);
  Multiplexer #(.enable("false")) multiplexer_1 (
    .in0(not_1_out), .in1(Opcode[1]), .out(multiplexer_1_out), .sel(Opcode[1]));
  not not_2 (not_2_out, Opcode[3]);
  not not_3 (not_3_out, Opcode[2]);
  not not_4 (not_4_out, Subop);
  not not_5 (not_5_out, Opcode[3]);
  not not_6 (not_6_out, Opcode[2]);
  not not_7 (not_7_out, Opcode[1]);
  not not_8 (not_8_out, Opcode[0]);
  not not_9 (not_9_out, Opcode[3]);
  not not_10 (not_10_out, Opcode[2]);
  not not_11 (not_11_out, Opcode[0]);
  not not_12 (not_12_out, Subop);
  not not_13 (not_13_out, Opcode[3]);
  not not_14 (not_14_out, Opcode[2]);
  not not_15 (not_15_out, Opcode[3]);
  not not_16 (not_16_out, Opcode[2]);
  not not_17 (not_17_out, Opcode[3]);
  not not_18 (not_18_out, Opcode[2]);
  not not_19 (not_19_out, Opcode[3]);
  not not_20 (not_20_out, Opcode[2]);
  not not_21 (not_21_out, Opcode[1]);
  and and_1 (ALUOperation[3], not_2_out, not_3_out, Opcode[1], Opcode[0], not_4_out);
  and and_2 (and_2_out, not_5_out, not_6_out, not_7_out, not_8_out, Subop);
  and and_3 (and_3_out, not_9_out, not_10_out, Opcode[1], not_11_out, not_12_out);
  buf and_4 (ALUOperation[1], not_13_out);  // AND_Gate
  and and_5 (and_5_out, not_15_out, not_16_out, multiplexer_1_out);
  and and_6 (and_6_out, not_17_out, not_18_out, Opcode[0]);
  and and_7 (ALUSrc, not_19_out, not_20_out, not_21_out, Opcode[0]);
  or or_1 (ALUOperation[2], and_2_out, and_3_out);
  or or_2 (RegWrite, and_5_out, and_6_out);

  assign ALUOperation[0] = 1'b0;
endmodule

module Arith_Log (
  input  Opcode3,
  input  Opcode2,
  input  Opcode1,
  input  Opcode0,
  input  Unsigned,
  input  Subop,
  output ALUOp3,
  output ALUOp2,
  output ALUOp1,
  output ALUOp0,
  output RegWrite,
  output ALUSrc
);

  wire and_2_out, and_3_out, and_5_out, and_6_out, not_1_out, not_2_out, not_3_out, not_4_out, not_5_out,
       not_6_out, not_7_out, not_8_out, not_9_out, not_10_out, not_11_out, not_12_out, not_13_out,
       not_14_out, not_15_out, not_16_out, not_17_out, not_18_out, not_19_out, not_20_out, not_21_out;

  not not_1 (not_1_out, Opcode3);
  not not_2 (not_2_out, Opcode2);
  not not_3 (not_3_out, Subop);
  not not_4 (not_4_out, Opcode3);
  not not_5 (not_5_out, Opcode2);
  not not_6 (not_6_out, Opcode1);
  not not_7 (not_7_out, Opcode0);
  not not_8 (not_8_out, Opcode3);
  not not_9 (not_9_out, Opcode2);
  not not_10 (not_10_out, Subop);
  not not_11 (not_11_out, Opcode3);
  not not_12 (not_12_out, Opcode2);
  not not_13 (not_13_out, Opcode1);
  not not_14 (not_14_out, Opcode3);
  not not_15 (not_15_out, Opcode2);
  not not_16 (not_16_out, Opcode1);
  not not_17 (not_17_out, Opcode3);
  not not_18 (not_18_out, Opcode2);
  not not_19 (not_19_out, Opcode3);
  not not_20 (not_20_out, Opcode2);
  not not_21 (not_21_out, Opcode1);
  and and_1 (ALUOp3, not_1_out, not_2_out, Opcode1, Opcode0, not_3_out);
  and and_2 (and_2_out, not_4_out, not_5_out, not_6_out, not_7_out, Subop);
  and and_3 (and_3_out, not_8_out, not_9_out, Opcode1, Opcode0, not_10_out);
  and and_4 (ALUOp1, not_11_out, not_12_out, not_13_out);
  and and_5 (and_5_out, not_14_out, not_15_out, not_16_out);
  and and_6 (and_6_out, not_17_out, not_18_out, Opcode0);
  and and_7 (ALUSrc, not_19_out, not_20_out, not_21_out, Opcode0);
  or or_1 (ALUOp2, and_2_out, and_3_out);
  or or_2 (RegWrite, and_5_out, and_6_out);

  assign ALUOp0 = 1'b0;
endmodule

module one_bit_ALU (
  input  Ainvert,
  input  Binvert,
  input  CarryIn,
  input  [1:0] Operation,
  input  a,
  input  b,
  input  Less,
  output Result,
  output Set,
  output CarryOut
);

  wire and_1_out, multiplexer_1_out, multiplexer_2_out, not_1_out, not_2_out, or_1_out;

  not not_1 (not_1_out, a);
  Multiplexer #(.enable("false")) multiplexer_1 (.in0(a), .in1(not_1_out), .out(multiplexer_1_out), .sel(Ainvert));
  not not_2 (not_2_out, b);
  Multiplexer #(.enable("false")) multiplexer_2 (.in0(b), .in1(not_2_out), .out(multiplexer_2_out), .sel(Binvert));
  and and_1 (and_1_out, multiplexer_1_out, multiplexer_2_out);
  or or_1 (or_1_out, multiplexer_1_out, multiplexer_2_out);
  Adder #(.width(1)) adder_1 (.a(multiplexer_1_out), .b(multiplexer_2_out), .out(Set), .cin(CarryIn), .cout(CarryOut));
  Multiplexer #(.select(2), .enable("false")) multiplexer_3 (
    .in0(and_1_out), .in1(or_1_out), .in2(Set), .in3(Less), .out(Result), .sel(Operation));
endmodule

module sixteen_bit_ALU (
  input  [3:0] ALUOperation,
  input  [15:0] a,
  input  [15:0] b,
  output Zero,
  output [15:0] Result,
  output Overflow
);

  wire one_bit_alu_1_carryout, one_bit_alu_2_carryout, one_bit_alu_3_carryout, one_bit_alu_4_carryout,
       one_bit_alu_5_carryout, one_bit_alu_6_carryout, one_bit_alu_7_carryout, one_bit_alu_8_carryout,
       one_bit_alu_9_carryout, one_bit_alu_10_carryout, one_bit_alu_11_carryout, one_bit_alu_12_carryout,
       one_bit_alu_13_carryout, one_bit_alu_14_carryout, one_bit_alu_15_carryout, one_bit_alu_16_carryout,
       one_bit_alu_16_set, xor_1_out;

  one_bit_ALU one_bit_alu_1 (
    .a(a[0]), .b(b[0]), .Less(xor_1_out), .Ainvert(ALUOperation[3]), .Binvert(ALUOperation[2]),
    .CarryIn(ALUOperation[2]), .Operation(ALUOperation[1:0]), .CarryOut(one_bit_alu_1_carryout),
    .Result(Result[0]));  // open: Set
  one_bit_ALU one_bit_alu_2 (
    .a(a[1]), .b(b[1]), .Less(1'b0), .Ainvert(ALUOperation[3]), .Binvert(ALUOperation[2]),
    .CarryIn(one_bit_alu_1_carryout), .Operation(ALUOperation[1:0]), .CarryOut(one_bit_alu_2_carryout),
    .Result(Result[1]));  // open: Set
  one_bit_ALU one_bit_alu_3 (
    .a(a[2]), .b(b[2]), .Less(1'b0), .Ainvert(ALUOperation[3]), .Binvert(ALUOperation[2]),
    .CarryIn(one_bit_alu_2_carryout), .Operation(ALUOperation[1:0]), .CarryOut(one_bit_alu_3_carryout),
    .Result(Result[2]));  // open: Set
  one_bit_ALU one_bit_alu_4 (
    .a(a[3]), .b(b[3]), .Less(1'b0), .Ainvert(ALUOperation[3]), .Binvert(ALUOperation[2]),
    .CarryIn(one_bit_alu_3_carryout), .Operation(ALUOperation[1:0]), .CarryOut(one_bit_alu_4_carryout),
    .Result(Result[3]));  // open: Set
  one_bit_ALU one_bit_alu_5 (
    .a(a[4]), .b(b[4]), .Less(1'b0), .Ainvert(ALUOperation[3]), .Binvert(ALUOperation[2]),
    .CarryIn(one_bit_alu_4_carryout), .Operation(ALUOperation[1:0]), .CarryOut(one_bit_alu_5_carryout),
    .Result(Result[4]));  // open: Set
  one_bit_ALU one_bit_alu_6 (
    .a(a[5]), .b(b[5]), .Less(1'b0), .Ainvert(ALUOperation[3]), .Binvert(ALUOperation[2]),
    .CarryIn(one_bit_alu_5_carryout), .Operation(ALUOperation[1:0]), .CarryOut(one_bit_alu_6_carryout),
    .Result(Result[5]));  // open: Set
  one_bit_ALU one_bit_alu_7 (
    .a(a[6]), .b(b[6]), .Less(1'b0), .Ainvert(ALUOperation[3]), .Binvert(ALUOperation[2]),
    .CarryIn(one_bit_alu_6_carryout), .Operation(ALUOperation[1:0]), .CarryOut(one_bit_alu_7_carryout),
    .Result(Result[6]));  // open: Set
  one_bit_ALU one_bit_alu_8 (
    .a(a[7]), .b(b[7]), .Less(1'b0), .Ainvert(ALUOperation[3]), .Binvert(ALUOperation[2]),
    .CarryIn(one_bit_alu_7_carryout), .Operation(ALUOperation[1:0]), .CarryOut(one_bit_alu_8_carryout),
    .Result(Result[7]));  // open: Set
  one_bit_ALU one_bit_alu_9 (
    .a(a[8]), .b(b[8]), .Less(1'b0), .Ainvert(ALUOperation[3]), .Binvert(ALUOperation[2]),
    .CarryIn(one_bit_alu_8_carryout), .Operation(ALUOperation[1:0]), .CarryOut(one_bit_alu_9_carryout),
    .Result(Result[8]));  // open: Set
  one_bit_ALU one_bit_alu_10 (
    .a(a[9]), .b(b[9]), .Less(1'b0), .Ainvert(ALUOperation[3]), .Binvert(ALUOperation[2]),
    .CarryIn(one_bit_alu_9_carryout), .Operation(ALUOperation[1:0]), .CarryOut(one_bit_alu_10_carryout),
    .Result(Result[9]));  // open: Set
  one_bit_ALU one_bit_alu_11 (
    .a(a[10]), .b(b[10]), .Less(1'b0), .Ainvert(ALUOperation[3]), .Binvert(ALUOperation[2]),
    .CarryIn(one_bit_alu_10_carryout), .Operation(ALUOperation[1:0]), .CarryOut(one_bit_alu_11_carryout),
    .Result(Result[10]));  // open: Set
  one_bit_ALU one_bit_alu_12 (
    .a(a[11]), .b(b[11]), .Less(1'b0), .Ainvert(ALUOperation[3]), .Binvert(ALUOperation[2]),
    .CarryIn(one_bit_alu_11_carryout), .Operation(ALUOperation[1:0]), .CarryOut(one_bit_alu_12_carryout),
    .Result(Result[11]));  // open: Set
  one_bit_ALU one_bit_alu_13 (
    .a(a[12]), .b(b[12]), .Less(1'b0), .Ainvert(ALUOperation[3]), .Binvert(ALUOperation[2]),
    .CarryIn(one_bit_alu_12_carryout), .Operation(ALUOperation[1:0]), .CarryOut(one_bit_alu_13_carryout),
    .Result(Result[12]));  // open: Set
  one_bit_ALU one_bit_alu_14 (
    .a(a[13]), .b(b[13]), .Less(1'b0), .Ainvert(ALUOperation[3]), .Binvert(ALUOperation[2]),
    .CarryIn(one_bit_alu_13_carryout), .Operation(ALUOperation[1:0]), .CarryOut(one_bit_alu_14_carryout),
    .Result(Result[13]));  // open: Set
  one_bit_ALU one_bit_alu_15 (
    .a(a[14]), .b(b[14]), .Less(1'b0), .Ainvert(ALUOperation[3]), .Binvert(ALUOperation[2]),
    .CarryIn(one_bit_alu_14_carryout), .Operation(ALUOperation[1:0]), .CarryOut(one_bit_alu_15_carryout),
    .Result(Result[14]));  // open: Set
  one_bit_ALU one_bit_alu_16 (
    .a(a[15]), .b(b[15]), .Less(1'b0), .Ainvert(ALUOperation[3]), .Binvert(ALUOperation[2]),
    .CarryIn(one_bit_alu_15_carryout), .Operation(ALUOperation[1:0]), .CarryOut(one_bit_alu_16_carryout),
    .Result(Result[15]), .Set(one_bit_alu_16_set));
  xor xor_1 (xor_1_out, one_bit_alu_16_set, Overflow);
  xor xor_2 (Overflow, one_bit_alu_15_carryout, one_bit_alu_16_carryout);
  nor nor_1 (Zero, Result[0], Result[1], Result[2], Result[3], Result[4], Result[5], Result[6], Result[7], Result[8], Result[9], Result[10], Result[11], Result[12], Result[13], Result[14], Result[15]);
endmodule

module PCDecoder (
  input  [3:0] Opcode,
  input  Subop,
  input  Zero,
  input  Less,
  output RegtoPC,
  output IMMtoPC,
  output ZerosToALU,
  output [3:0] ALUOp
);

  wire and_4_out, and_5_out, and_6_out, and_7_out, and_8_out, not_1_out, not_2_out, not_3_out, not_4_out,
       not_5_out, not_6_out, not_7_out, not_8_out, not_9_out, not_10_out, not_11_out, not_12_out, not_13_out,
       not_14_out, not_15_out, not_16_out;

  not not_1 (not_1_out, Opcode[2]);
  not not_2 (not_2_out, Opcode[1]);
  not not_3 (not_3_out, Subop);
  not not_4 (not_4_out, Opcode[2]);
  not not_5 (not_5_out, Opcode[1]);
  not not_6 (not_6_out, Opcode[0]);
  not not_7 (not_7_out, Opcode[2]);
  not not_8 (not_8_out, Opcode[1]);
  not not_9 (not_9_out, Zero);
  not not_10 (not_10_out, Opcode[2]);
  not not_11 (not_11_out, Zero);
  not not_12 (not_12_out, Opcode[0]);
  not not_13 (not_13_out, Zero);
  not not_14 (not_14_out, Less);
  not not_15 (not_15_out, Opcode[0]);
  and and_1 (ZerosToALU, Opcode[3], not_16_out);
  not not_16 (not_16_out, Opcode[2]);
  and and_2 (ALUOp[1], Opcode[3], not_1_out);
  and and_3 (RegtoPC, Opcode[3], Opcode[2], not_2_out, Opcode[0], not_3_out);
  and and_4 (and_4_out, Opcode[3], not_4_out, not_5_out, not_6_out, Zero);
  and and_5 (and_5_out, Opcode[3], not_7_out, not_8_out, Opcode[0], not_9_out);
  and and_6 (and_6_out, Opcode[3], not_10_out, Opcode[0], not_11_out, Less);
  and and_7 (and_7_out, Opcode[3], Opcode[1], not_12_out, not_13_out, not_14_out);
  and and_8 (and_8_out, Opcode[3], Opcode[2], Opcode[1], not_15_out);
  or or_1 (IMMtoPC, and_4_out, and_5_out, and_6_out, and_7_out, and_8_out);

  assign {ALUOp[3:2], ALUOp[0]} = 3'b000;
endmodule

module PCDecoderLogic (
  input  Opcode3,
  input  Opcode2,
  input  Opcode1,
  input  Opcode0,
  input  Subop,
  input  Zero,
  input  Less,
  output RegtoPC,
  output IMMtoPC,
  output OnestoALU
);

  wire and_2_out, and_3_out, and_4_out, and_5_out, and_6_out, not_1_out, not_2_out, not_3_out, not_4_out,
       not_5_out, not_6_out, not_7_out, not_8_out, not_9_out, not_10_out, not_11_out, not_12_out, not_13_out,
       not_14_out, not_15_out;

  not not_1 (not_1_out, Opcode1);
  not not_2 (not_2_out, Subop);
  not not_3 (not_3_out, Opcode2);
  not not_4 (not_4_out, Opcode1);
  not not_5 (not_5_out, Opcode0);
  not not_6 (not_6_out, Opcode2);
  not not_7 (not_7_out, Opcode1);
  not not_8 (not_8_out, Zero);
  not not_9 (not_9_out, Opcode2);
  not not_10 (not_10_out, Zero);
  not not_11 (not_11_out, Opcode0);
  not not_12 (not_12_out, Zero);
  not not_13 (not_13_out, Less);
  not not_14 (not_14_out, Opcode0);
  not not_15 (not_15_out, Opcode2);
  and and_1 (RegtoPC, Opcode3, Opcode2, not_1_out, Opcode0, not_2_out);
  and and_2 (and_2_out, Opcode3, not_3_out, not_4_out, not_5_out, Zero);
  and and_3 (and_3_out, Opcode3, not_6_out, not_7_out, Opcode0, not_8_out);
  and and_4 (and_4_out, Opcode3, not_9_out, Opcode0, not_10_out, Less);
  and and_5 (and_5_out, Opcode3, Opcode1, not_11_out, not_12_out, not_13_out);
  and and_6 (and_6_out, Opcode3, Opcode2, Opcode1, not_14_out);
  and and_7 (OnestoALU, Opcode3, not_15_out);
  or or_1 (IMMtoPC, and_2_out, and_3_out, and_4_out, and_5_out, and_6_out);
endmodule

module Decoder (
  input  [3:0] Opcode,
  input  Subop,
  input  Zero,
  input  Less,
  output ShiftSrc,
  output ShifterToReg,
  output RegWrite,
  output [3:0] ALUOp,
  output IMMtoALU,
  output RegtoPC,
  output IMMtoPC,
  output ZerosToALU,
  output MemWrite,
  output MemtoReg,
  output Halt,
  output LED,
  output WriteLED,
  output MemRead,
  output PCtoReg
);

  wire Arith_LogDecoder_regwrite, JALDecoder_immtopc, JALDecoder_regwrite, MemDecoder_regwrite,
       PCDecoder_immtopc, ShifterDecoder_regwrite;
  wire [3:0] Arith_LogDecoder_aluoperation, PCDecoder_aluop;

  ShifterDecoder ShifterDecoder (
    .Opcode(Opcode), .ShiftSrc(ShiftSrc), .ShiftertoReg(ShifterToReg), .RegWrite(ShifterDecoder_regwrite));
  Arith_Log_Decoder Arith_LogDecoder (
    .Opcode(Opcode), .Subop(Subop), .ALUOperation(Arith_LogDecoder_aluoperation),
    .RegWrite(Arith_LogDecoder_regwrite), .ALUSrc(IMMtoALU));
  PCDecoder PCDecoder (
    .Opcode(Opcode), .Subop(Subop), .Zero(Zero), .Less(Less), .RegtoPC(RegtoPC), .IMMtoPC(PCDecoder_immtopc),
    .ZerosToALU(ZerosToALU), .ALUOp(PCDecoder_aluop));
  MemDecoder MemDecoder (
    .Opcode(Opcode), .Subop(Subop), .MemWrite(MemWrite), .MemtoReg(MemtoReg), .RegWrite(MemDecoder_regwrite),
    .MemRead(MemRead));
  HaltDecoder haltdecoder_1 (.Opcode(Opcode), .LED(LED));  // open: Halt
  PutDecoder PutDecoder (.Opcode(Opcode), .WriteLED(WriteLED));
  JALDecoder JALDecoder (
    .Opcode(Opcode), .IMMtoPC(JALDecoder_immtopc), .PCtoReg(PCtoReg), .RegWrite(JALDecoder_regwrite));
  or or_1 (RegWrite, ShifterDecoder_regwrite, Arith_LogDecoder_regwrite, MemDecoder_regwrite, JALDecoder_regwrite);
  or or_2 (IMMtoPC, PCDecoder_immtopc, JALDecoder_immtopc);
  assign ALUOp = Arith_LogDecoder_aluoperation | PCDecoder_aluop;  // OR_Gate or_3, 4 bits wide
endmodule

module MemDecoder (
  input  [3:0] Opcode,
  input  Subop,
  output MemWrite,
  output MemtoReg,
  output RegWrite,
  output MemRead
);

  and and_1 (MemWrite, ~Opcode[0], Opcode[1], Opcode[2], ~Opcode[3], Subop);  // AND_Gate
  and and_2 (MemRead, ~Opcode[0], Opcode[1], Opcode[2], ~Opcode[3], ~Subop);  // AND_Gate

  assign MemtoReg = MemRead;
  assign RegWrite = MemRead;
endmodule

module HaltDecoder_Yasser (
  input  [15:0] Opcode,
  output Halt,
  output LED
);

  and and_1 (Halt, ~Opcode[15], Opcode[14], Opcode[13], Opcode[12]);  // AND_Gate

  assign LED = Halt;
endmodule

module PutDecoder (
  input  [3:0] Opcode,
  output WriteLED
);

  and and_1 (WriteLED, Opcode[0], Opcode[1], Opcode[2], Opcode[3]);
endmodule

module JALDecoder (
  input  [3:0] Opcode,
  output IMMtoPC,
  output PCtoReg,
  output RegWrite
);

  and and_1 (IMMtoPC, ~Opcode[0], ~Opcode[1], Opcode[2], Opcode[3]);  // AND_Gate

  assign PCtoReg = IMMtoPC;
  assign RegWrite = IMMtoPC;
endmodule

module ResultToLess (
  input  [15:0] Result,
  output Less
);


  assign Less = Result[15];
endmodule

module side (
  input  Op3,
  input  Op2,
  input  Op1,
  input  Op0,
  output Op3_2,
  output Op2_2,
  output Op1_2,
  output Op0_2
);

  wire not_1_out;

  and and_1 (Op1_2, Op3, not_1_out);
  not not_1 (not_1_out, Op2);

  assign Op0_2 = 1'b0;
  assign Op2_2 = 1'b0;
  assign Op3_2 = 1'b0;
endmodule

module IF_ID (
  input  [15:0] From_Instruction_Memory,
  input  Clock,
  input  Bubble,
  output [15:0] To_Instruction_Splitter
);

  Register #(.width(16)) register_1 (
    .D(From_Instruction_Memory), .Q(To_Instruction_Splitter), .clk(Clock), .clr(Bubble));  // open: en
endmodule

module ID_EX (
  input  [2:0] ShiftSrc_IN,
  input  [15:0] Register1_IN,
  input  ShifterToReg_IN,
  input  [15:0] Register2_IN,
  input  [15:0] SignExtended_IN,
  input  [3:0] ALUop_IN,
  input  IMMtoALU_IN,
  input  [7:0] Immediate_IN,
  input  RegtoPC_IN,
  input  IMMtoPC_IN,
  input  [7:0] PC_1_IN,
  input  ZerosToALU_IN,
  input  MemWrite_IN,
  input  MemToReg_IN,
  input  [3:0] ShiftAmount_IN,
  input  Halt_IN,
  input  SubOp_IN,
  input  LED_IN,
  input  WriteLED_IN,
  input  [2:0] RS_IN,
  input  MemRead_IN,
  input  [3:0] OPCode_IN,
  input  PCtoReg_IN,
  input  WriteEn_IN,
  input  clk,
  output [2:0] RS2_OUT,
  output [15:0] Register1_OUT,
  output ShifterToReg_OUT,
  output [15:0] Register2_OUT,
  output [15:0] SignExtended_OUT,
  output [3:0] ALUop_OUT,
  output IMMtoALU_OUT,
  output [7:0] Immediate_OUT,
  output RegtoPC_OUT,
  output IMMtoPC_OUT,
  output [7:0] PC_1_OUT,
  output ZerosToALU_OUT,
  output MemWrite_OUT,
  output MemToReg_OUT,
  output [3:0] ShiftAmount_OUT,
  output Halt_OUT,
  output SubOp_OUT,
  output LED_OUT,
  output WriteLED_OUT,
  output [2:0] RS_OUT,
  output MemRead_OUT,
  output [3:0] OPCode_OUT,
  output PCtoReg_OUT,
  output WriteEn_OUT
);

  Register #(.width(3)) register_1 (.D(ShiftSrc_IN), .Q(RS2_OUT), .clk(clk));  // open: en, clr
  Register #(.width(1)) register_2 (.D(ShifterToReg_IN), .Q(ShifterToReg_OUT), .clk(clk));  // open: en, clr
  Register #(.width(4)) register_3 (.D(ALUop_IN), .Q(ALUop_OUT), .clk(clk));  // open: en, clr
  Register #(.width(1)) register_4 (.D(IMMtoALU_IN), .Q(IMMtoALU_OUT), .clk(clk));  // open: en, clr
  Register #(.width(1)) register_5 (.D(RegtoPC_IN), .Q(RegtoPC_OUT), .clk(clk));  // open: en, clr
  Register #(.width(1)) register_6 (.D(IMMtoPC_IN), .Q(IMMtoPC_OUT), .clk(clk));  // open: en, clr
  Register #(.width(1)) register_7 (.D(ZerosToALU_IN), .Q(ZerosToALU_OUT), .clk(clk));  // open: en, clr
  Register #(.width(1)) register_8 (.D(MemWrite_IN), .Q(MemWrite_OUT), .clk(clk));  // open: en, clr
  Register #(.width(1)) register_9 (.D(MemToReg_IN), .Q(MemToReg_OUT), .clk(clk));  // open: en, clr
  Register #(.width(1)) register_10 (.D(Halt_IN), .Q(Halt_OUT), .clk(clk));  // open: en, clr
  Register #(.width(1)) register_11 (.D(LED_IN), .Q(LED_OUT), .clk(clk));  // open: en, clr
  Register #(.width(1)) register_12 (.D(WriteLED_IN), .Q(WriteLED_OUT), .clk(clk));  // open: en, clr
  Register #(.width(1)) register_13 (.D(MemRead_IN), .Q(MemRead_OUT), .clk(clk));  // open: en, clr
  Register #(.width(1)) register_14 (.D(PCtoReg_IN), .Q(PCtoReg_OUT), .clk(clk));  // open: en, clr
  Register #(.width(16)) register_15 (.D(Register1_IN), .Q(Register1_OUT), .clk(clk));  // open: en, clr
  Register #(.width(16)) register_16 (.D(Register2_IN), .Q(Register2_OUT), .clk(clk));  // open: en, clr
  Register #(.width(16)) register_17 (.D(SignExtended_IN), .Q(SignExtended_OUT), .clk(clk));  // open: en, clr
  Register register_18 (.D(Immediate_IN), .Q(Immediate_OUT), .clk(clk));  // open: en, clr
  Register register_19 (.D(PC_1_IN), .Q(PC_1_OUT), .clk(clk));  // open: en, clr
  Register #(.width(4)) register_20 (.D(ShiftAmount_IN), .Q(ShiftAmount_OUT), .clk(clk));  // open: en, clr
  Register #(.width(1)) register_21 (.D(SubOp_IN), .Q(SubOp_OUT), .clk(clk));  // open: en, clr
  Register #(.width(3)) register_22 (.D(RS_IN), .Q(RS_OUT), .clk(clk));  // open: en, clr
  Register #(.width(4)) register_23 (.D(OPCode_IN), .Q(OPCode_OUT), .clk(clk));  // open: en, clr
  Register #(.width(1)) register_24 (.D(WriteEn_IN), .Q(WriteEn_OUT), .clk(clk));  // open: en, clr
endmodule

module EX_MEM (
  input  [15:0] Register1_IN,
  input  [2:0] RS2_IN,
  input  [15:0] ALUResult_IN,
  input  ShifterToReg_IN,
  input  [15:0] Register2_IN,
  input  [7:0] PCD_IN,
  input  MemWrite_IN,
  input  MemToReg_IN,
  input  [3:0] ShiftAmount_IN,
  input  SubOp_IN,
  input  LED_IN,
  input  WriteLED_IN,
  input  ALU0_IN,
  input  MemRead_IN,
  input  [7:0] PC_1_IN,
  input  PCtoReg_IN,
  input  [2:0] RS_IN,
  input  clk,
  input  WriteEn_IN,
  output [15:0] Register1_OUT,
  output [2:0] RS2_OUT,
  output [15:0] ALUResult_OUT,
  output ShifterToReg_OUT,
  output [15:0] Register2_OUT,
  output [7:0] PCD_OUT,
  output MemWrite_OUT,
  output MemToReg_OUT,
  output [3:0] ShiftAmount_OUT,
  output SubOp_OUT,
  output LED_OUT,
  output WriteLED_OUT,
  output ALU0_OUT,
  output MemRead_OUT,
  output [7:0] PC_1_OUT,
  output PCtoReg_OUT,
  output [2:0] RS_OUT,
  output WriteEn_OUT
);

  Register #(.width(3)) register_1 (.D(RS2_IN), .Q(RS2_OUT), .clk(clk));  // open: en, clr
  Register #(.width(1)) register_2 (.D(MemWrite_IN), .Q(MemWrite_OUT), .clk(clk));  // open: en, clr
  Register #(.width(1)) register_3 (.D(MemToReg_IN), .Q(MemToReg_OUT), .clk(clk));  // open: en, clr
  Register #(.width(1)) register_4 (.D(LED_IN), .Q(LED_OUT), .clk(clk));  // open: en, clr
  Register #(.width(1)) register_5 (.D(WriteLED_IN), .Q(WriteLED_OUT), .clk(clk));  // open: en, clr
  Register #(.width(1)) register_6 (.D(MemRead_IN), .Q(MemRead_OUT), .clk(clk));  // open: en, clr
  Register #(.width(1)) register_7 (.D(PCtoReg_IN), .Q(PCtoReg_OUT), .clk(clk));  // open: en, clr
  Register #(.width(1)) register_8 (.D(ShifterToReg_IN), .Q(ShifterToReg_OUT), .clk(clk));  // open: en, clr
  Register #(.width(16)) register_9 (.D(Register1_IN), .Q(Register1_OUT), .clk(clk));  // open: en, clr
  Register #(.width(16)) register_10 (.D(ALUResult_IN), .Q(ALUResult_OUT), .clk(clk));  // open: en, clr
  Register #(.width(16)) register_11 (.D(Register2_IN), .Q(Register2_OUT), .clk(clk));  // open: en, clr
  Register register_12 (.D(PCD_IN), .Q(PCD_OUT), .clk(clk));  // open: en, clr
  Register #(.width(4)) register_13 (.D(ShiftAmount_IN), .Q(ShiftAmount_OUT), .clk(clk));  // open: en, clr
  Register #(.width(1)) register_14 (.D(SubOp_IN), .Q(SubOp_OUT), .clk(clk));  // open: en, clr
  Register #(.width(1)) register_15 (.D(ALU0_IN), .Q(ALU0_OUT), .clk(clk));  // open: en, clr
  Register register_16 (.D(PC_1_IN), .Q(PC_1_OUT), .clk(clk));  // open: en, clr
  Register #(.width(3)) register_17 (.D(RS_IN), .Q(RS_OUT), .clk(clk));  // open: en, clr
  Register #(.width(1)) register_18 (.D(WriteEn_IN), .Q(WriteEn_OUT), .clk(clk));  // open: en, clr
endmodule

module MEM_WB (
  input  [15:0] Data_IN,
  input  [15:0] ALUResult_IN,
  input  ShifterToReg_IN,
  input  [15:0] Shifter_IN,
  input  [7:0] PCD_IN,
  input  [15:0] Extender_IN,
  input  LED_IN,
  input  MemToReg_IN,
  input  [15:0] Register1_IN,
  input  WriteLED_IN,
  input  [2:0] RS_IN,
  input  MemRead_IN,
  input  WriteEn_IN,
  input  clk,
  output [15:0] Data_OUT,
  output [15:0] ALUResult_OUT,
  output ShifterToReg_OUT,
  output [15:0] Shifter_OUT,
  output [7:0] PCD_OUT,
  output [15:0] Extender_OUT,
  output LED_OUT,
  output MemToReg_OUT,
  output [15:0] Register1_OUT,
  output WriteLED_OUT,
  output [2:0] RS_OUT,
  output MemRead_OUT,
  output WriteEn_OUT
);

  Register #(.width(1)) register_1 (.D(ShifterToReg_IN), .Q(ShifterToReg_OUT), .clk(clk));  // open: en, clr
  Register register_2 (.D(PCD_IN), .Q(PCD_OUT), .clk(clk));  // open: en, clr
  Register #(.width(1)) register_3 (.D(LED_IN), .Q(LED_OUT), .clk(clk));  // open: en, clr
  Register #(.width(1)) register_4 (.D(MemToReg_IN), .Q(MemToReg_OUT), .clk(clk));  // open: en, clr
  Register #(.width(1)) register_5 (.D(WriteLED_IN), .Q(WriteLED_OUT), .clk(clk));  // open: en, clr
  Register #(.width(1)) register_6 (.D(MemRead_IN), .Q(MemRead_OUT), .clk(clk));  // open: en, clr
  Register #(.width(16)) register_7 (.D(Data_IN), .Q(Data_OUT), .clk(clk));  // open: en, clr
  Register #(.width(16)) register_8 (.D(ALUResult_IN), .Q(ALUResult_OUT), .clk(clk));  // open: en, clr
  Register #(.width(16)) register_9 (.D(Shifter_IN), .Q(Shifter_OUT), .clk(clk));  // open: en, clr
  Register #(.width(16)) register_10 (.D(Extender_IN), .Q(Extender_OUT), .clk(clk));  // open: en, clr
  Register #(.width(16)) register_11 (.D(Register1_IN), .Q(Register1_OUT), .clk(clk));  // open: en, clr
  Register #(.width(3)) register_12 (.D(RS_IN), .Q(RS_OUT), .clk(clk));  // open: en, clr
  Register #(.width(1)) register_13 (.D(WriteEn_IN), .Q(WriteEn_OUT), .clk(clk));  // open: en, clr
endmodule

module BranchCheck (
  input  [15:0] RS,
  input  [3:0] OPCode,
  output BranchTaken
);

  wire comparator_1_eq;

  Comparator #(.width(16)) comparator_1 (.a(RS), .b({16{1'b0}}), .eq(comparator_1_eq));  // open: gt, lt
  BranchCheckDecoder branchcheckdecoder_1 (
    .Zero(comparator_1_eq), .OPCode0(OPCode[0]), .OPCode1(OPCode[1]), .OpCode2(OPCode[2]),
    .OPCode3(OPCode[3]), .BranchTake(BranchTaken));
endmodule

module BranchCheckDecoder (
  input  Zero,
  input  OPCode0,
  input  OPCode1,
  input  OpCode2,
  input  OPCode3,
  output BranchTake
);

  wire and_1_out, and_2_out, not_1_out, not_2_out, not_3_out, not_4_out, not_5_out, not_6_out;

  not not_1 (not_1_out, Zero);
  not not_2 (not_2_out, OPCode0);
  not not_3 (not_3_out, OpCode2);
  not not_4 (not_4_out, OPCode0);
  not not_5 (not_5_out, OPCode1);
  not not_6 (not_6_out, OpCode2);
  and and_1 (and_1_out, not_1_out, not_2_out, OPCode1, not_3_out, OPCode3);
  and and_2 (and_2_out, Zero, not_4_out, not_5_out, not_6_out, OPCode3);
  or or_1 (BranchTake, and_1_out, and_2_out);
endmodule

module ForwardingUnit (
  input  [15:0] IDEXRegister1_IN,
  input  [15:0] MEMWBData_IN,
  input  [2:0] IDEXRS_IN,
  input  [2:0] MEMWBRS_IN,
  output [15:0] Register1_OUT
);

  wire comparator_1_eq;

  Comparator #(.width(3)) comparator_1 (.a(IDEXRS_IN), .b(MEMWBRS_IN), .eq(comparator_1_eq));  // open: gt, lt
  Multiplexer #(.width(16), .enable("false")) multiplexer_1 (
    .in0(IDEXRegister1_IN), .in1(MEMWBData_IN), .out(Register1_OUT), .sel(comparator_1_eq));
endmodule

module HaltDecoder (
  input  [3:0] Opcode,
  output Halt,
  output LED
);

  and and_1 (Halt, ~Opcode[3], Opcode[2], Opcode[1], Opcode[0]);  // AND_Gate

  assign LED = Halt;
endmodule

module ForwardDetector (
  input  registerwrite,
  input  [2:0] WriteReg,
  input  [2:0] Rs,
  output \output 
);

  wire comparator_1_eq;

  Comparator #(.width(3), .mode("unsigned")) comparator_1 (.a(WriteReg), .b(Rs), .eq(comparator_1_eq));  // open: gt, lt
  and and_1 (\output , registerwrite, comparator_1_eq);
endmodule

module ForwardingUnit_Main (
  input  [2:0] ID_Ex_rs1,
  input  [2:0] ID_EX_rs2,
  input  ex_memRegWrite,
  input  [2:0] ex_memWBREG,
  input  mem_wbRegWrite,
  input  [2:0] mem_wbWBREG,
  output [1:0] ToMuxA,
  output [1:0] ToMuxB
);

  ForwardDetector forwarddetector_1 (
    .registerwrite(ex_memRegWrite), .WriteReg(ex_memWBREG), .Rs(ID_Ex_rs1), .\output (ToMuxA[1]));
  ForwardDetector forwarddetector_2 (
    .registerwrite(ex_memRegWrite), .WriteReg(ex_memWBREG), .Rs(ID_EX_rs2), .\output (ToMuxB[1]));
  ForwardDetector forwarddetector_3 (
    .registerwrite(mem_wbRegWrite), .WriteReg(mem_wbWBREG), .Rs(ID_Ex_rs1), .\output (ToMuxA[0]));
  ForwardDetector forwarddetector_4 (
    .registerwrite(mem_wbRegWrite), .WriteReg(mem_wbWBREG), .Rs(ID_EX_rs2), .\output (ToMuxB[0]));
endmodule

module StoreForwardingUnit (
  input  mem_wb_memtoreg,
  input  [2:0] mem_wb_WBREG,
  input  [2:0] ex_mem_rs2,
  input  Ex_Mem_memwrite,
  output ToWriteDataMux
);

  wire and_1_out, and_2_out, comparator_1_eq;

  Comparator #(.width(3)) comparator_1 (.a(mem_wb_WBREG), .b(ex_mem_rs2), .eq(comparator_1_eq));  // open: gt, lt
  and and_1 (and_1_out, mem_wb_memtoreg, comparator_1_eq);
  and and_2 (and_2_out, and_1_out, Ex_Mem_memwrite);
  not not_1 (ToWriteDataMux, and_2_out);
endmodule
